# Fritzing sketch ChickenDoor (saved by Fritzing 0.9.4)
circuit board: 8.48706cm x 5.84835cm
breadboards: 1

parts:
  Part1 = Itsy Bitsy 32u4 5V @ 16MHz [part_number="Adafruit #3677"]
  JACK1 = 2.1mm DC Barrel Jack
  Door_Lock = Solenoid
  Light_Meter = Adafruit GA1A1S202WP [part_number="Adafruit #1384"]
  s-door-closed = Pushbutton [package=THT]
  s-door-open = Pushbutton [package=THT]
  IC1 = L293D [package=THT]
  IC2 = L293D [package=THT]
  M1 = Stepper Motor - Bipolar
  S1 = SPST Switch [package=switch-spdt_lock.007s]

nets:
  GND: Part1.GND, JACK1.switch, Light_Meter.GND, s-door-closed.leg1, s-door-open.leg1, IC1.0V, IC2.0V, S1.P
  N1: Part1.VBAT, JACK1.center, IC1.+Vmotor, IC2.+Vmotor
  N2: Part1.D12, IC1.In_1
  N3: Part1.D11, IC1.In_2
  N4: Part1.D10, IC1.In_3
  N5: Part1.D9, IC1.In_4
  N6: Part1.D5, IC2.In_3
  N7: Part1.SCL, IC2.In_4
  N8: Part1.D0, IC1.Enable_1, IC1.Enable_2, IC2.Enable_1, IC2.Enable_2
  3.3V: Part1.3.3V, Light_Meter.VCC
  N9: Part1.A5, S1.O
  N10: Part1.A4, S1.S
  N11: Part1.A3, Light_Meter.OUT
  N12: Part1.A2, s-door-open.leg0
  N13: Part1.A1, s-door-closed.leg0
  N14: Part1.+5V, IC1.+V, IC2.+V
  N15: Door_Lock.pin1, IC2.Out_3_(_Controlled_by_Enable_2_)
  N16: Door_Lock.pin2, IC2.Out_4_(_Controlled_by_Enable_2_)
  N17: IC1.Out_1_(_Controlled_by_Enable_1_), M1.A
  N18: IC1.Out_2_(_Controlled_by_Enable_1_), M1.C
  N19: IC1.Out_3_(_Controlled_by_Enable_2_), M1.B
  N20: IC1.Out_4_(_Controlled_by_Enable_2_), M1.D

notes:
  Red Yellow Grey Green
  12 11 10 9

custom parts:
  Itsy Bitsy 32u4 5V @ 16MHz: What's smaller than a Feather but larger than a Trinket? It's an Itsy Bitsy! Small, powerful, Arduino-compatible - this microcontroller board is perfect when you want something very compact, but still with a bunch of pins. Itsy Bitsy is only 1.4" long by 0.7" wide, but has 6 power pins, 6 analog & digital pins and 17 digital pins. It packs much of the same capability as an Arduino UNO. So it's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
  2.1mm DC Barrel Jack: 2.1mm DC Barrel Jack with Thru-Hole Connectors (breadboardable)
  Adafruit GA1A1S202WP: Upgrade a project that uses a photocell with the GA1A12S202 analog light sensor. Like a CdS photo-cell, the sensor does not require a microcontroller, the analog voltage output increases with the amount of light shining on the sensor face. This sensor has a lot of improvements that make it better for nearly any project. The biggest improvement over plain photocells is a true log-lin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
